# Fritzing sketch Sketch (saved by Fritzing 0.9.3b)
breadboards: 1

parts:
  부품1 = Arduino Uno (Rev3)
  4digit_FND = 7-SEGMENT-4DIGIT-YOUNGSUN [package=7-segment-4digit-youngsun-longpads]
  R1 = Resistor [tolerance=±5% resistance=220 package=THT]
  R2 = Resistor [tolerance=±5% resistance=220 package=THT]
  R3 = Resistor [tolerance=±5% resistance=220 package=THT]
  R4 = Resistor [tolerance=±5% resistance=220 package=THT]
  초음파센서 = hc-sr04
  IR_수신기 = IR Receiver Breakout [package=PCB]

nets:
  N1: 부품1.A0, R4.Pin_1
  N2: 부품1.A1, 초음파센서.Trig
  N3: 부품1.A4/SDA, R2.Pin_1
  N4: 부품1.A5/SCL, R1.Pin_1
  N5: 부품1.D8, 4digit_FND.DIG2
  N6: 부품1.D9_PWM, 4digit_FND.C
  N7: 부품1.D10_PWM/SS, 4digit_FND.DIG3
  N8: 부품1.D11_PWM/MOSI, 4digit_FND.COL-A
  N9: 부품1.D12/MISO, R3.Pin_1
  N10: 부품1.D2, IR_수신기.OUT
  N11: 부품1.D3_PWM, 초음파센서.Echo
  N12: 부품1.D4, 4digit_FND.A
  N13: 부품1.D5_PWM, 4digit_FND.APOS-A
  N14: 부품1.D6_PWM, 4digit_FND.E
  N15: 부품1.D7, 4digit_FND.D
  VCC: 부품1.5V, 초음파센서.VCC, IR_수신기.VCC
  GND: 부품1.GND, 초음파센서.GND, IR_수신기.GND
  N16: 4digit_FND.DP, R4.Pin_0
  N17: 4digit_FND.F, R3.Pin_0
  N18: 4digit_FND.COL-C, R2.Pin_0
  N19: 4digit_FND.G, R1.Pin_0
